# Fritzing sketch energy-monitor-cpbr7 (saved by Fritzing 0.8.3b)
breadboards: 1

parts:
  Part1 = Arduino Uno (Rev3)  # not connected
  Part3 = Arduino Ethernet Shield (Rev3)
  R1 = Resistor [tolerance=±5% resistance=33 package=THT]
  CT1 = Audio Jack (TRS) 3.5mm [package="PG203J [THT]"]
  C1 = Electrolytic Capacitor [capacitance=10µF package="100 mil [THT, electrolytic]"]
  R3 = Resistor [tolerance=±5% resistance=470k package=THT]
  R2 = Resistor [tolerance=±5% resistance=470k package=THT]

nets:
  N1: Part3.A0, R1.Pin_1, CT1.Tip
  N2: Part3.5V, R3.Pin_0
  N3: Part3.GND, C1.-, R2.Pin_0
  N4: R1.Pin_0, CT1.Sleeve, C1.+, R3.Pin_1, R2.Pin_1
